// Logisim project Single Cycle Processor.circ as structural Verilog: 14 circuits, main circuit main
module main (
  input  Reset,
  output [4:0] out_2,
  output [3:0] out_3,
  output [31:0] out_4,
  output [31:0] out_5,
  output out_6,
  output out_7,
  output out_8,
  output out_9,
  output out_10,
  output out_11,
  output out_12,
  output [1:0] out_13,
  output out_14,
  output [1:0] out_15,
  output [3:0] out_16,
  output out_17
);

  wire [1:0] Reg_Src;
  wire [3:0] A1, A2, A3, IW__3_0, IW__15_12, multiplexer_4_out;
  wire [23:0] IW__23_0;
  wire [31:0] adder_2_out, alu_1_result, data_memory_1_rd, IM_iw, multiplexer_1_out, multiplexer_5_out,
       multiplexer_7_out, multiplexer_8_out, PC, PC_4, r0, r1, r2, r3, r4, r5, r6, r7, r8, r9, r10, r11, r12,
       r13, r14, r15, register_file_1_rd, register_file_1_rn;

  Clock clock_1 (.out(out_8));
  Multiplexer #(.width(32), .disabled(0), .enable("false")) multiplexer_1 (
    .in0(PC_4), .in1(out_5), .out(multiplexer_1_out), .sel(out_7));
  Register #(.width(32)) u_PC (.D(multiplexer_1_out), .Q(PC), .clk(out_8), .clr(Reset));  // open: en
  // Probe on r0
  // Probe on r1
  // Probe on r2
  // Probe on r3
  // Probe on r4
  // Probe on r5
  Instruction_Memory IM (.A(PC), .IW(IM_iw));
  Adder #(.width(32)) adder_1 (.a(PC), .b(32'h4), .out(PC_4));  // open: cin, cout
  IW IW (.IW(IM_iw), ._3_0(IW__3_0), ._15_12(IW__15_12), ._19_16(out_3), ._23_0(IW__23_0));
  Adder #(.width(32)) adder_2 (.a(PC_4), .b(32'h4), .out(adder_2_out));  // open: cin, cout
  // Probe on r6
  // Probe on r7
  // Probe on r8
  // Probe on r9
  // Probe on r10
  // Probe on r11
  Control_Unit Control_Unit (
    .ALU_Flags(out_16), .IW(IM_iw), .MemToReg(out_9), .ALU_Src(out_11), .Reg_Src(Reg_Src), .Imm_src(out_13),
    .ALU_Control(out_15), .Reg_W(out_6), .PC_Src(out_7), .Funct_4_0(out_2), .CLK(out_8), .MemW(out_12),
    .Mov(out_14), .BL(out_10), .Bx(out_17));
  Multiplexer #(.width(4), .disabled(0), .enable("false")) multiplexer_2 (
    .in0(out_3), .in1(4'b1111), .out(A1), .sel(Reg_Src[0]));
  Multiplexer #(.width(4), .disabled(0), .enable("false")) multiplexer_3 (
    .in0(IW__3_0), .in1(IW__15_12), .out(A2), .sel(Reg_Src[1]));
  Multiplexer #(.width(4), .disabled(0), .enable("false")) multiplexer_4 (
    .in0(IW__15_12), .in1(4'b1111), .out(multiplexer_4_out), .sel(out_17));
  Multiplexer #(.width(32), .enable("false")) multiplexer_5 (
    .in0(adder_2_out), .in1(r14), .out(multiplexer_5_out), .sel(out_17));
  Multiplexer #(.width(4), .disabled(0), .enable("false")) multiplexer_6 (
    .in0(multiplexer_4_out), .in1(4'b1110), .out(A3), .sel(out_10));
  Multiplexer #(.width(32), .enable("false")) multiplexer_7 (
    .in0(out_5), .in1(PC_4), .out(multiplexer_7_out), .sel(out_10));
  // Probe on r12
  // Probe on r13
  // Probe on r14
  // Probe on r15
  // Probe on out_4
  Extend Extend (._23_0(IW__23_0), .Imm_Src(out_13), .out_3(out_4));
  Register_File register_file_1 (
    .A3__RD(A3), .WD3(multiplexer_7_out), .R15(multiplexer_5_out), .WE3(out_6), .CLK(out_8), .Reset(Reset),
    .R0(r0), .R1(r1), .R2(r2), .R3(r3), .R4(r4), .R5(r5), .R6(r6), .R7(r7), .R8(r8), .R9(r9), .R10(r10),
    .R11(r11), .R12(r12), .R13(r13), .R14(r14), .R15_2(r15), .A1(A1), .A2(A2), .RD(register_file_1_rd),
    .RN(register_file_1_rn));
  Multiplexer #(.width(32), .disabled(0), .enable("false")) multiplexer_8 (
    .in0(register_file_1_rn), .in1(out_4), .out(multiplexer_8_out), .sel(out_11));
  // Probe on Reg_Src
  // Probe on out_5
  // Probe on A1
  // Probe on A2
  // Probe on A3
  // Probe on PC
  ALU alu_1 (
    .Control(out_15), .ALU_Flag(out_16), .A__RD(register_file_1_rd), .B__RN(multiplexer_8_out),
    .Result(alu_1_result), .Mov(out_14));
  Data_Memory data_memory_1 (
    .ALU_Result(alu_1_result), .WD(register_file_1_rn), .RD(data_memory_1_rd), .CLK(out_8), .WE(out_12),
    .Reset(Reset));
  Multiplexer #(.width(32), .disabled(0), .enable("false")) multiplexer_9 (
    .in0(alu_1_result), .in1(data_memory_1_rd), .out(out_5), .sel(out_9));

  // Other names for the same wires on the sheet: ALU_Control[1:0] = out_15; ALU_Flags[3:0] = out_16; ALU_Src = out_11;
  //   BL = out_10; Bx = out_17; CLK = out_8; Imm_Src[1:0] = out_13; MemToReg = out_9; MemW = out_12; Mov = out_14;
  //   PC_Src = out_7; Reg_Src_0 = Reg_Src[0]; Reg_Src_1 = Reg_Src[1]; Reg_W = out_6

  // Notes on the sheet:
  //   A1
  //   A2
  //   A3 (RD)
  //   WD3
  //   Register File
  //   ALU
  //   Data Memory
endmodule

module ALU (
  input  [31:0] A__RD,
  input  [31:0] B__RN,
  input  Mov,
  input  [1:0] Control,
  output [31:0] Result,
  output [3:0] ALU_Flag
);

  wire adder_1_cout, not_1_out, xnor_1_out, xor_1_out;
  wire [31:0] adder_1_out, and_3_out, multiplexer_1_out, multiplexer_2_out, not_2_out, not_3_out, or_1_out;

  Multiplexer #(.width(32), .disabled(0), .enable("false")) multiplexer_1 (
    .in0(A__RD), .in1({32{1'b0}}), .out(multiplexer_1_out), .sel(Mov));
  not not_1 (not_1_out, Control[1]);
  and and_1 (ALU_Flag[1], not_1_out, adder_1_cout);
  assign not_2_out = ~B__RN;  // NOT_Gate not_2, 32 bits wide
  Multiplexer #(.width(32), .disabled(0), .enable("false")) multiplexer_2 (
    .in0(B__RN), .in1(not_2_out), .out(multiplexer_2_out), .sel(Control[0]));
  Adder #(.width(32)) adder_1 (
    .a(multiplexer_1_out), .b(multiplexer_2_out), .out(adder_1_out), .cin(Control[0]), .cout(adder_1_cout));
  and and_2 (ALU_Flag[2], not_3_out[0], not_3_out[1], not_3_out[2], not_3_out[3], not_3_out[4], not_3_out[5], not_3_out[6], not_3_out[7], not_3_out[8], not_3_out[9], not_3_out[10], not_3_out[11], not_3_out[12], not_3_out[13], not_3_out[14], not_3_out[15], not_3_out[17], not_3_out[18], not_3_out[19], not_3_out[20], not_3_out[21], not_3_out[22], not_3_out[23], not_3_out[24], not_3_out[25], not_3_out[26], not_3_out[27], not_3_out[28], not_3_out[29], not_3_out[30], not_3_out[31], not_3_out[16]);
  assign and_3_out = multiplexer_1_out & B__RN;  // AND_Gate and_3, 32 bits wide
  assign or_1_out = multiplexer_1_out | B__RN;  // OR_Gate or_1, 32 bits wide
  Multiplexer #(.select(2), .width(32), .disabled(0), .enable("false")) multiplexer_3 (
    .in0(adder_1_out), .in1(adder_1_out), .in2(and_3_out), .in3(or_1_out), .out({ALU_Flag[3], Result[30:0]}),
    .sel(Control));
  assign not_3_out = ~{ALU_Flag[3], Result[30:0]};  // NOT_Gate not_3, 32 bits wide
  xor xor_1 (xor_1_out, multiplexer_1_out[31], adder_1_out[31]);
  NotExactlyOne xnor_1 (.out(xnor_1_out), .in1(B__RN[31]), .in2(Control[0]), .in3(multiplexer_1_out[31]));
  and and_4 (ALU_Flag[0], xnor_1_out, xor_1_out, not_1_out);

  assign Result[31] = ALU_Flag[3];

  // Notes on the sheet:
  //   C
  //   N
  //   Z
  //   NZCV
  //   V
endmodule

module Instruction_Memory (
  input  [31:0] A,
  output [31:0] IW
);

  // Probe on A
  ROM #(.dataWidth(32)) rom_1 (.addr(A[9:2]), .data(IW), .sel(1'b1));
  // Probe on IW

  // Notes on the sheet:
  //   contents of rom_1 (hex, n*v repeats v):
  //   e3a0d080 e3a00014 eb000000 eafffffe e24dd004 e58d4000 e3a01000 e3a02001 e3a03000 e3a04000 e1540000
  //   ca000009 e3540001 da000004 e0823001 e1a01002 e1a02003 e2844001 eafffff6 e1a03004 e2844001 eafffff3
  //   e59d4000 e28dd004 e1a00003 e12fff1e
endmodule

module Control_Unit (
  input  [3:0] ALU_Flags,
  input  CLK,
  input  [31:0] IW,
  output BL,
  output PC_Src,
  output Reg_W,
  output MemW,
  output MemToReg,
  output ALU_Src,
  output [1:0] Reg_Src,
  output [1:0] Imm_src,
  output [1:0] ALU_Control,
  output Bx,
  output Mov,
  output [4:0] Funct_4_0
);

  wire comparator_1_eq, decoder_1_mem_w, decoder_1_nowrite, decoder_1_pcs, decoder_1_reg_w, or_1_out;
  wire [1:0] decoder_1_flag_w;

  // Probe on IW[27:4]
  Decoder decoder_1 (
    .Op(IW[27:26]), .Funct(IW[25:20]), .Rd(IW[15:12]), .Bx_Compare(comparator_1_eq),
    .ALU_Control(ALU_Control), .Flag_W(decoder_1_flag_w), .PCS(decoder_1_pcs), .MemtoReg(MemToReg),
    .ALU_src(ALU_Src), .Mem_W(decoder_1_mem_w), .Reg_W(decoder_1_reg_w), .Reg_src(Reg_Src),
    .Imm_src(Imm_src), .Funct_4_0(Funct_4_0), .NoWrite(decoder_1_nowrite), .Mov(Mov), .BL(BL), .Bx(Bx));
  Comparator #(.width(24)) comparator_1 (.a(IW[27:4]), .b(24'h12fff1), .eq(comparator_1_eq));  // open: gt, lt
  or or_1 (or_1_out, Bx, decoder_1_pcs);
  Conditional_Logic conditional_logic_1 (
    .PC_Src(or_1_out), .Reg_W(decoder_1_reg_w), .NoWrite(decoder_1_nowrite), .Mem_W(decoder_1_mem_w),
    .Flag_W(decoder_1_flag_w), .CLK(CLK), .Cond(IW[31:28]), .ALU_Flag(ALU_Flags), .PC_Src_2(PC_Src),
    .Reg_W_2(Reg_W), .MemW(MemW));

  // Notes on the sheet:
  //   op = 27:26
endmodule

module Decoder (
  input  [1:0] Op,
  input  [5:0] Funct,
  input  [3:0] Rd,
  input  Bx_Compare,
  output BL,
  output PCS,
  output MemtoReg,
  output ALU_src,
  output Mem_W,
  output Reg_W,
  output [1:0] Reg_src,
  output [1:0] Imm_src,
  output Bx,
  output [1:0] ALU_Control,
  output NoWrite,
  output [1:0] Flag_W,
  output Mov,
  output [4:0] Funct_4_0
);

  wire alu_decoder_1_mov, main_decoder_1_aluop, main_decoder_1_b, main_decoder_1_regw;

  Main_Decoder main_decoder_1 (
    .Op(Op), .Func_0(Funct[0]), .Func_5(Funct[5]), .Bx_Compare(Bx_Compare), .B(main_decoder_1_b),
    .MemtoReg__M2R(MemtoReg), .MemW(Mem_W), .ALU_source(ALU_src), .Imm_Source(Imm_src),
    .RegW(main_decoder_1_regw), .Reg_source(Reg_src), .ALUop(main_decoder_1_aluop), .Bx(Bx));
  PC_Logic pc_logic_1 (.Rd(Rd), .Reg_W(main_decoder_1_regw), .Branch(main_decoder_1_b), .PCs(PCS));
  ALU_Decoder alu_decoder_1 (
    .ALU_Op(main_decoder_1_aluop), .Funct_4_0(Funct[4:0]), .ALU_Control(ALU_Control), .Flag_W(Flag_W),
    .NoWrite(NoWrite), .Mov(alu_decoder_1_mov));
  or or_1 (Mov, alu_decoder_1_mov, Bx);
  and and_1 (BL, Funct[4], main_decoder_1_b);
  or or_2 (Reg_W, BL, main_decoder_1_regw);

  assign Funct_4_0 = Funct[4:0];
endmodule

module Main_Decoder (
  input  [1:0] Op,
  input  Func_0,
  input  Func_5,
  input  Bx_Compare,
  output B,
  output MemtoReg__M2R,
  output MemW,
  output ALU_source,
  output [1:0] Imm_Source,
  output RegW,
  output [1:0] Reg_source,
  output ALUop,
  output Bx
);

  wire DP_Imm_out, DP_Reg_out;

  and DP_Reg (DP_Reg_out, ~Op[1], ~Op[0], ~Func_5, ~Bx_Compare);  // AND_Gate
  and DP_Imm (DP_Imm_out, ~Op[1], ~Op[0], Func_5, ~Bx_Compare);  // AND_Gate
  and STR (MemW, ~Op[1], Op[0], ~Func_0, ~Bx_Compare);  // AND_Gate
  and LDR (MemtoReg__M2R, ~Op[1], Op[0], Func_0, ~Bx_Compare);  // AND_Gate
  and u_B (B, Op[1], ~Op[0], ~Bx_Compare);  // AND_Gate
  or or_1 (ALU_source, DP_Imm_out, MemW, MemtoReg__M2R, B);
  or or_2 (Imm_Source[0], MemW, MemtoReg__M2R);
  or or_3 (RegW, DP_Reg_out, DP_Imm_out, MemtoReg__M2R);
  or or_4 (ALUop, DP_Reg_out, DP_Imm_out);

  assign Bx = Bx_Compare;
  assign Imm_Source[1] = B;
  assign Reg_source = {MemW, B};

  // Notes on the sheet:
  //   Op1
  //   Funct 5
  //   Bx
  //   Op0
  //   Funct 0
  //   Reg
  //   Imm
  //   LDR
  //   STR
  //   B
endmodule

module PC_Logic (
  input  [3:0] Rd,
  input  Reg_W,
  input  Branch,
  output PCs
);

  wire and_1_out, comparator_1_eq;

  Comparator #(.width(4), .mode("unsigned")) comparator_1 (.a(Rd), .b(4'b1111), .eq(comparator_1_eq));  // open: gt, lt
  and and_1 (and_1_out, comparator_1_eq, Reg_W);
  or or_1 (PCs, and_1_out, Branch);
endmodule

module ALU_Decoder (
  input  ALU_Op,
  input  [4:0] Funct_4_0,
  output [1:0] ALU_Control,
  output [1:0] Flag_W,
  output NoWrite,
  output Mov
);

  wire ADD_out, AND_out, or_1_out, or_2_out, or_5_out, ORR_out, SUB_out;

  and ADD (ADD_out, ~Funct_4_0[4], Funct_4_0[3], ~Funct_4_0[2], ~Funct_4_0[1], ALU_Op);  // AND_Gate
  and SUB (SUB_out, ~Funct_4_0[4], ~Funct_4_0[3], Funct_4_0[2], ~Funct_4_0[1], ALU_Op);  // AND_Gate
  and AND (AND_out, ~Funct_4_0[4], ~Funct_4_0[3], ~Funct_4_0[2], ~Funct_4_0[1], ALU_Op);  // AND_Gate
  and ORR (ORR_out, Funct_4_0[4], Funct_4_0[3], ~Funct_4_0[2], ~Funct_4_0[1], ALU_Op);  // AND_Gate
  and and_2 (Flag_W[1], Funct_4_0[0], ALU_Op);
  and CMP (NoWrite, Funct_4_0[4], ~Funct_4_0[3], Funct_4_0[2], ~Funct_4_0[1], Funct_4_0[0], ALU_Op);  // AND_Gate
  and u_MOV (Mov, Funct_4_0[4], Funct_4_0[3], ~Funct_4_0[2], Funct_4_0[1], ALU_Op);  // AND_Gate
  or or_1 (or_1_out, ADD_out, Mov);
  or or_2 (or_2_out, SUB_out, or_1_out);
  or or_3 (ALU_Control[0], SUB_out, NoWrite, ORR_out);
  or or_4 (ALU_Control[1], AND_out, ORR_out);
  and and_3 (Flag_W[0], or_5_out, Flag_W[1]);
  or or_5 (or_5_out, or_2_out, NoWrite);
endmodule

module Register_File (
  input  WE3,
  input  CLK,
  input  Reset,
  input  [3:0] A3__RD,
  input  [31:0] WD3,
  input  [31:0] R15,
  input  [3:0] A1,
  input  [3:0] A2,
  output [31:0] R0,
  output [31:0] R1,
  output [31:0] R2,
  output [31:0] R3,
  output [31:0] R4,
  output [31:0] R5,
  output [31:0] R6,
  output [31:0] R7,
  output [31:0] R8,
  output [31:0] R9,
  output [31:0] R10,
  output [31:0] R11,
  output [31:0] RD,
  output [31:0] RN,
  output [31:0] R12,
  output [31:0] R13,
  output [31:0] R14,
  output [31:0] R15_2
);

  wire decoder_1_out0, decoder_1_out1, decoder_1_out2, decoder_1_out3, decoder_1_out4, decoder_1_out5,
       decoder_1_out6, decoder_1_out7, decoder_1_out8, decoder_1_out9, decoder_1_out10, decoder_1_out11,
       decoder_1_out12, decoder_1_out13, decoder_1_out14;

  Decoder_part #(.select(4), .disabled(0)) decoder_1 (
    .out0(decoder_1_out0), .out1(decoder_1_out1), .out2(decoder_1_out2), .out3(decoder_1_out3),
    .out4(decoder_1_out4), .out5(decoder_1_out5), .out6(decoder_1_out6), .out7(decoder_1_out7),
    .out8(decoder_1_out8), .out9(decoder_1_out9), .out10(decoder_1_out10), .out11(decoder_1_out11),
    .out12(decoder_1_out12), .out13(decoder_1_out13), .out14(decoder_1_out14), .sel(A3__RD), .en(WE3));  // open: out15
  Register #(.width(32)) u_R0 (.D(WD3), .en(decoder_1_out0), .Q(R0), .clk(CLK), .clr(Reset));
  Register #(.width(32)) u_R1 (.D(WD3), .en(decoder_1_out1), .Q(R1), .clk(CLK), .clr(Reset));
  Register #(.width(32)) u_R2 (.D(WD3), .en(decoder_1_out2), .Q(R2), .clk(CLK), .clr(Reset));
  Register #(.width(32)) u_R3 (.D(WD3), .en(decoder_1_out3), .Q(R3), .clk(CLK), .clr(Reset));
  Register #(.width(32)) u_R4 (.D(WD3), .en(decoder_1_out4), .Q(R4), .clk(CLK), .clr(Reset));
  Register #(.width(32)) u_R5 (.D(WD3), .en(decoder_1_out5), .Q(R5), .clk(CLK), .clr(Reset));
  Register #(.width(32)) u_R6 (.D(WD3), .en(decoder_1_out6), .Q(R6), .clk(CLK), .clr(Reset));
  Register #(.width(32)) u_R7 (.D(WD3), .en(decoder_1_out7), .Q(R7), .clk(CLK), .clr(Reset));
  Register #(.width(32)) u_R8 (.D(WD3), .en(decoder_1_out8), .Q(R8), .clk(CLK), .clr(Reset));
  Register #(.width(32)) u_R9 (.D(WD3), .en(decoder_1_out9), .Q(R9), .clk(CLK), .clr(Reset));
  Register #(.width(32)) u_R10 (.D(WD3), .en(decoder_1_out10), .Q(R10), .clk(CLK), .clr(Reset));
  Register #(.width(32)) u_R11 (.D(WD3), .en(decoder_1_out11), .Q(R11), .clk(CLK), .clr(Reset));
  Register #(.width(32)) u_R12 (.D(WD3), .en(decoder_1_out12), .Q(R12), .clk(CLK), .clr(Reset));
  Register #(.width(32)) u_R13 (.D(WD3), .en(decoder_1_out13), .Q(R13), .clk(CLK), .clr(Reset));
  Register #(.width(32)) u_R14 (.D(WD3), .en(decoder_1_out14), .Q(R14), .clk(CLK), .clr(Reset));
  Multiplexer #(.select(4), .width(32), .disabled(0), .enable("false")) multiplexer_1 (
    .in0(R0), .in1(R1), .in2(R2), .in3(R3), .in4(R4), .in5(R5), .in6(R6), .in7(R7), .in8(R8), .in9(R9),
    .in10(R10), .in11(R11), .in12(R12), .in13(R13), .in14(R14), .in15(R15), .out(RD), .sel(A1));
  Multiplexer #(.select(4), .width(32), .disabled(0), .enable("false")) multiplexer_2 (
    .in0(R0), .in1(R1), .in2(R2), .in3(R3), .in4(R4), .in5(R5), .in6(R6), .in7(R7), .in8(R8), .in9(R9),
    .in10(R10), .in11(R11), .in12(R12), .in13(R13), .in14(R14), .in15(R15), .out(RN), .sel(A2));

  assign R15_2 = R15;
endmodule

module Conditional_Logic (
  input  PC_Src,
  input  Reg_W,
  input  NoWrite,
  input  Mem_W,
  input  [1:0] Flag_W,
  input  CLK,
  input  [3:0] Cond,
  input  [3:0] ALU_Flag,
  output PC_Src_2,
  output Reg_W_2,
  output MemW
);

  wire and_1_out, and_2_out, check_condition_1_cond_ex;
  wire [1:0] CV_q, NZ_q;

  Register #(.width(2)) NZ (.D(ALU_Flag[3:2]), .en(and_1_out), .Q(NZ_q), .clk(CLK));  // open: clr
  Register #(.width(2)) CV (.D(ALU_Flag[1:0]), .en(and_2_out), .Q(CV_q), .clk(CLK));  // open: clr
  and and_1 (and_1_out, Flag_W[1], check_condition_1_cond_ex);
  and and_2 (and_2_out, Flag_W[0], check_condition_1_cond_ex);
  Check_Condition check_condition_1 (.Cond(Cond), .NZ(NZ_q), .CV(CV_q), .Cond_Ex(check_condition_1_cond_ex));
  and and_3 (PC_Src_2, PC_Src, check_condition_1_cond_ex);
  and and_4 (Reg_W_2, Reg_W, ~NoWrite, check_condition_1_cond_ex);  // AND_Gate
  and and_5 (MemW, Mem_W, check_condition_1_cond_ex);

  // Notes on the sheet:
  //   3:2 = NZ
  //   1:0 = CV
endmodule

module Data_Memory (
  input  CLK,
  input  Reset,
  input  [31:0] ALU_Result,
  input  WE,
  input  [31:0] WD,
  output [31:0] RD
);

  wire not_1_out;

  // Probe on ALU_Result
  RAM #(.dataWidth(32), .bus("separate")) ram_1 (
    .addr(ALU_Result[9:2]), .din(WD), .data(RD), .str(WE), .sel(1'b1), .clk(CLK), .ld(not_1_out), .clr(Reset));
  not not_1 (not_1_out, WE);
  // Probe on RD
endmodule

module IW (
  input  [31:0] IW,
  output [3:0] _3_0,
  output [3:0] _15_12,
  output [3:0] _19_16,
  output [23:0] _23_0
);


  assign _3_0 = IW[3:0];
  assign _15_12 = IW[15:12];
  assign _19_16 = IW[19:16];
  assign _23_0 = IW[23:0];
endmodule

module Extend (
  input  [23:0] _23_0,
  input  [1:0] Imm_Src,
  output [31:0] out_3
);

  // Probe on {{7{_23_0[23]}}, _23_0[22:0], 2'b00}
  // Probe on {{24{1'b0}}, _23_0[7:0]}
  // Probe on {{20{1'b0}}, _23_0[11:0]}
  Multiplexer #(.select(2), .width(32), .disabled(0), .enable("false")) multiplexer_1 (
    .in0({{24{1'b0}}, _23_0[7:0]}), .in1({{20{1'b0}}, _23_0[11:0]}),
    .in2({{7{_23_0[23]}}, _23_0[22:0], 2'b00}), .out(out_3), .sel(Imm_Src));  // open: in3
endmodule

module Check_Condition (
  input  [3:0] Cond,
  input  [1:0] NZ,
  input  [1:0] CV,
  output Cond_Ex
);

  wire AL_out, and_1_out, Equal_out, GT_out, LE_out, LT_out, or_1_out, xnor_1_out, xor_1_out, xor_2_out;

  xor xor_1 (xor_1_out, NZ[1], CV[0]);
  xnor xnor_1 (xnor_1_out, NZ[1], CV[0]);
  xor xor_2 (xor_2_out, NZ[1], CV[0]);
  and Equal (Equal_out, ~Cond[3], ~Cond[2], ~Cond[1], ~Cond[0], NZ[0]);  // AND_Gate
  and and_1 (and_1_out, ~NZ[0], xnor_1_out);  // AND_Gate
  or or_1 (or_1_out, NZ[0], xor_2_out);
  and LT (LT_out, Cond[3], ~Cond[2], Cond[1], Cond[0], xor_1_out);  // AND_Gate
  and GT (GT_out, Cond[3], Cond[2], ~Cond[1], ~Cond[0], and_1_out);  // AND_Gate
  and LE (LE_out, Cond[3], Cond[2], ~Cond[1], Cond[0], or_1_out);  // AND_Gate
  and AL (AL_out, Cond[3], Cond[2], Cond[1], ~Cond[0]);  // AND_Gate
  or or_2 (Cond_Ex, Equal_out, LT_out, GT_out, LE_out, AL_out);

  // Notes on the sheet:
  //   N
  //   Z
  //   3
  //   V
  //   C
  //   1
  //   2
  //   0
endmodule
